# Fritzing sketch lightshow (saved by Fritzing 0.9.3b)
breadboards: 1

parts:
  R1 = Resistor [tolerance=±5% power=0.25W resistance=220 package=THT]
  Part1 = Arduino Nano (Rev3.0) (ICSP)
  LED2 = LED - 5mm [color="Infrared (880nm)" current=0.030A package="5 mm [THT]"]
  LED3 = LED - 5mm [color="Green (555nm)" current=0.030A package="5 mm [THT]"]
  LED4 = LED - 5mm [color="Yellow (592nm)" current=0.030A package="5 mm [THT]"]
  LED5 = LED - 5mm [color="Green (555nm)" current=0.030A package="5 mm [THT]"]
  LED6 = LED - 5mm [color="Green (555nm)" current=0.030A package="5 mm [THT]"]
  R2 = Resistor [tolerance=±5% power=0.25W resistance=220 package=THT]
  R3 = Resistor [tolerance=±5% power=0.25W resistance=220 package=THT]
  R4 = Resistor [tolerance=±5% power=0.25W resistance=220 package=THT]
  R5 = Resistor [tolerance=±5% power=0.25W resistance=220 package=THT]
  R6 = Resistor [tolerance=±5% power=0.25W resistance=220 package=THT]
  S2 = Pushbutton [package="[THT]"]
  LED7 = LED - 5mm [color="Red (633nm)" current=0.030A package="5 mm [THT]"]
  R8 = Resistor [tolerance=±5% power=0.25W resistance=220 package=THT]
  J1 = Basic Servo
  LED8 = LED - 5mm [color="Yellow (595nm)" current=0.030A package="5 mm [THT]"]
  R9 = Resistor [tolerance=±5% power=0.25W resistance=220 package=THT]
  LED1 = LED - 5mm [color="Infrared (850nm)" current=0.030A package="5 mm [THT]"]
  R10 = Rotary Potentiometer (Small) [maximum_resistance=100kΩ package=THT]

nets:
  N1: R1.Pin_0, LED1.cathode
  GND: R1.Pin_1, Part1.GND, R2.Pin_1, R3.Pin_1, R4.Pin_1, R5.Pin_1, R6.Pin_1, S2.Pin_3, S2.Pin_4, R8.Pin_1, J1.gnd, R9.Pin_1, R10.leg1
  N2: Part1.D2, LED7.anode
  N3: Part1.D3, J1.pulse
  N4: Part1.D4, S2.Pin_1, S2.Pin_2
  N5: Part1.D7, LED8.anode
  N6: Part1.D8, LED4.anode
  N7: Part1.D9, LED6.anode
  N8: Part1.D10, LED5.anode
  N9: Part1.D11/MOSI, LED3.anode
  N10: Part1.D12/MISO, LED2.anode
  5V: Part1.5V, J1.vcc, R10.leg2
  N11: Part1.A0, R10.wiper
  N12: Part1.D13/SCK, LED1.anode
  N13: LED2.cathode, R2.Pin_0
  N14: LED3.cathode, R4.Pin_0
  N15: LED4.cathode, R5.Pin_0
  N16: LED5.cathode, R3.Pin_0
  N17: LED6.cathode, R6.Pin_0
  N18: LED7.cathode, R8.Pin_0
  N19: LED8.cathode, R9.Pin_0

notes:
  10K Potentiometer
  Microcontroller
  LED's
  220 Ohm resistors
  Push Button
